# Fritzing sketch Cansat esquema electrico (saved by Fritzing 0.9.3b)

parts:
  ARDUINO_NANO = Arduino Nano (Rev3.0)
  BMP280 = BMP280
  APC220 = APC220 with antenna
  MPU = MPU-6050 Board GY-521 [form="♀ (female)" package=THT]
  BN-220 = bn-220- GPS-module
  VCC1 = Battery block 9V

nets:
  N1: ARDUINO_NANO.D2, BN-220.pin_2
  N2: ARDUINO_NANO.D3, BN-220.pin_3
  N3: ARDUINO_NANO.D10, APC220.TXD
  N4: ARDUINO_NANO.D11/MOSI, APC220.RXD
  N5: ARDUINO_NANO.VIN, VCC1.+
  GND: ARDUINO_NANO.GND, BMP280.GND, APC220.GND, MPU.pin2, BN-220.pin_1, VCC1.-
  5V: ARDUINO_NANO.5V, BMP280.VIN, APC220.VCC, MPU.pin1, BN-220.pin_4
  N6: ARDUINO_NANO.A5, BMP280.SCL, MPU.pin3
  N7: ARDUINO_NANO.A4, BMP280.SDA, MPU.pin4

custom parts:
  BMP280: Temperature Humidity Barometric presure Sensor, I2C
  APC220 with antenna: Radio transceiver module for Arduino operating in the 418-455MHz band.
  MPU-6050 Board GY-521: Acelerometro y Giroscopio MPU-6050 Board GY-521
  bn-220- GPS-module: bn-220l GPS module. Chipset : 8030-KT Receiving Format : GPS,GLONASS,Galileo,BeiDou,QZSS and SBAS
  Battery block 9V: 9 Volt battery block with 200mil pcb footprint spacing
